// Logisim project alu.circ as structural Verilog: 2 circuits, main circuit alu
module alu (
  input  [31:0] A,
  input  [31:0] B,
  input  [3:0] ALUSel,
  output [31:0] Result
);

  wire add_sel, and_sel, b_sel, comparator_1_lt, divu_sel, mul_sel, mulh_sel, mulhu_sel, or_sel, remu_sel,
       sll_sel, slt_sel, sra_sel, srl_sel, sub_sel, unknown_sel, xor_sel;
  wire [31:0] add0, and0, divu0, mul0, mulh0, mulhu0, multiplexer_2_out, multiplexer_3_out,
       multiplexer_4_out, multiplexer_5_out, multiplexer_6_out, multiplexer_7_out, multiplexer_8_out,
       multiplexer_9_out, multiplexer_10_out, multiplexer_11_out, multiplexer_12_out, multiplexer_13_out,
       multiplexer_14_out, multiplexer_15_out, or0, remu0, sll0, slt0, sra0, srl0, sub0, xor0;

  Decoder #(.select(4), .enable("false")) decoder_1 (
    .out0(add_sel), .out1(and_sel), .out2(or_sel), .out3(xor_sel), .out4(srl_sel), .out5(sra_sel),
    .out6(sll_sel), .out7(slt_sel), .out8(divu_sel), .out9(remu_sel), .out10(mul_sel), .out11(mulhu_sel),
    .out12(sub_sel), .out13(b_sel), .out14(mulh_sel), .out15(unknown_sel), .sel(ALUSel));
  Adder #(.width(32)) adder_1 (.a(A), .b(B), .out(add0));  // open: cin, cout
  assign and0 = A & B;  // AND_Gate and_1, 32 bits wide
  assign or0 = A | B;  // OR_Gate or_1, 32 bits wide
  assign xor0 = A ^ B;  // XOR_Gate xor_1, 32 bits wide
  Shifter #(.width(32), .shift("lr")) shifter_1 (.in(A), .\dist (B[4:0]), .out(srl0));
  Shifter #(.width(32), .shift("ar")) shifter_2 (.in(A), .\dist (B[4:0]), .out(sra0));
  Shifter #(.width(32)) shifter_3 (.in(A), .\dist (B[4:0]), .out(sll0));
  Comparator #(.width(32)) comparator_1 (.a(A), .b(B), .lt(comparator_1_lt));  // open: gt, eq
  Divider #(.width(32)) divider_1 (.a(A), .b(B), .out(divu0), .rem(remu0));  // open: upper
  Multiplier #(.width(32)) multiplier_1 (.a(A), .b(B), .out(mul0), .cout(mulhu0));  // open: cin
  Subtractor #(.width(32)) subtractor_1 (.a(A), .b(B), .out(sub0));  // open: bin, bout
  Multiplexer #(.width(32), .enable("false")) multiplexer_1 (
    .in0({32{1'b0}}), .in1(32'h1), .out(slt0), .sel(comparator_1_lt));
  mulh_circ mulh_circ_1 (.mulh_A(mulhu0), .mulh_B(A), .mulh_in(B), .mulh_out(mulh0));
  // Probe on mulh0
  Multiplexer #(.width(32), .enable("false")) multiplexer_2 (
    .in0({32{1'b0}}), .in1(add0), .out(multiplexer_2_out), .sel(add_sel));
  Multiplexer #(.width(32), .enable("false")) multiplexer_3 (
    .in0(multiplexer_2_out), .in1(and0), .out(multiplexer_3_out), .sel(and_sel));
  Multiplexer #(.width(32), .enable("false")) multiplexer_4 (
    .in0(multiplexer_3_out), .in1(or0), .out(multiplexer_4_out), .sel(or_sel));
  Multiplexer #(.width(32), .enable("false")) multiplexer_5 (
    .in0(multiplexer_4_out), .in1(xor0), .out(multiplexer_5_out), .sel(xor_sel));
  Multiplexer #(.width(32), .enable("false")) multiplexer_6 (
    .in0(multiplexer_5_out), .in1(srl0), .out(multiplexer_6_out), .sel(srl_sel));
  Multiplexer #(.width(32), .enable("false")) multiplexer_7 (
    .in0(multiplexer_6_out), .in1(sra0), .out(multiplexer_7_out), .sel(sra_sel));
  Multiplexer #(.width(32), .enable("false")) multiplexer_8 (
    .in0(multiplexer_7_out), .in1(sll0), .out(multiplexer_8_out), .sel(sll_sel));
  Multiplexer #(.width(32), .enable("false")) multiplexer_9 (
    .in0(multiplexer_8_out), .in1(slt0), .out(multiplexer_9_out), .sel(slt_sel));
  Multiplexer #(.width(32), .enable("false")) multiplexer_10 (
    .in0(multiplexer_9_out), .in1(divu0), .out(multiplexer_10_out), .sel(divu_sel));
  Multiplexer #(.width(32), .enable("false")) multiplexer_11 (
    .in0(multiplexer_10_out), .in1(remu0), .out(multiplexer_11_out), .sel(remu_sel));
  Multiplexer #(.width(32), .enable("false")) multiplexer_12 (
    .in0(multiplexer_11_out), .in1(mul0), .out(multiplexer_12_out), .sel(mul_sel));
  Multiplexer #(.width(32), .enable("false")) multiplexer_13 (
    .in0(multiplexer_12_out), .in1(mulhu0), .out(multiplexer_13_out), .sel(mulhu_sel));
  Multiplexer #(.width(32), .enable("false")) multiplexer_14 (
    .in0(multiplexer_13_out), .in1(sub0), .out(multiplexer_14_out), .sel(sub_sel));
  Multiplexer #(.width(32), .enable("false")) multiplexer_15 (
    .in0(multiplexer_14_out), .in1(B), .out(multiplexer_15_out), .sel(b_sel));
  Multiplexer #(.width(32), .enable("false")) multiplexer_16 (
    .in0(multiplexer_15_out), .in1(mulh0), .out(Result), .sel(mulh_sel));

  // Other names for the same wires on the sheet: bsel0[31:0] = B

  // Notes on the sheet:
  //   INPUTS to your circuit
  //   DON'T CHANGE THE LOCATIONS OF THE INPUTS AND OUTPUTS!
  //   OUTPUT from your circuit
endmodule

module mulh_circ (
  input  [31:0] mulh_A,
  input  [31:0] mulh_B,
  input  [31:0] mulh_in,
  output [31:0] mulh_out
);

  wire A_negative, A_positive, AB_negative, AB_positive, not_3_out, not_4_out, not_5_out, not_6_out;
  wire [31:0] adder_1_out, adder_2_out, multiplexer_1_out, multiplexer_2_out, multiplexer_3_out,
       multiplier_1_cout, multiplier_1_out, not_1_out, not_2_out;

  // Probe on mulh_in
  assign not_1_out = ~mulh_in;  // NOT_Gate not_1, 32 bits wide
  // Probe on mulh_B
  assign not_2_out = ~mulh_in;  // NOT_Gate not_2, 32 bits wide
  not not_3 (not_3_out, mulh_A[31]);
  not not_4 (not_4_out, mulh_B[31]);
  not not_5 (not_5_out, mulh_B[31]);
  not not_6 (not_6_out, mulh_A[31]);
  // Probe on not_2_out
  Adder #(.width(32)) adder_1 (.a({1'b1, mulh_in[30:0]}), .b(32'h1), .out(adder_1_out));  // open: cin, cout
  Adder #(.width(32)) adder_2 (.a({1'b1, not_1_out[30:0]}), .b(32'h1), .out(adder_2_out));  // open: cin, cout
  // Probe on mulh_A
  and A_B_negative (AB_negative, mulh_A[31], mulh_B[31]);
  and A_B_positive (AB_positive, not_3_out, not_4_out);
  and u_A_negative (A_negative, mulh_A[31], not_5_out);
  and u_A_positive (A_positive, not_6_out, mulh_B[31]);
  // Probe on {1'b0, not_2_out[30:0]}
  // Probe on adder_1_out
  // Probe on multiplier_1_out
  Multiplier #(.width(32)) multiplier_1 (
    .a(mulh_A), .b(mulh_B), .out(multiplier_1_out), .cout(multiplier_1_cout));  // open: cin
  Multiplexer #(.width(32), .enable("false")) multiplexer_1 (
    .in0({32{1'b0}}), .in1({1'b0, not_2_out[30:0]}), .out(multiplexer_1_out), .sel(AB_negative));
  Multiplexer #(.width(32), .enable("false")) multiplexer_2 (
    .in0(multiplexer_1_out), .in1(mulh_in), .out(multiplexer_2_out), .sel(AB_negative));
  Multiplexer #(.width(32), .enable("false")) multiplexer_3 (
    .in0(multiplexer_2_out), .in1(adder_1_out), .out(multiplexer_3_out), .sel(A_positive));
  Multiplexer #(.width(32), .enable("false")) multiplexer_4 (
    .in0(multiplexer_3_out), .in1(adder_2_out), .out(mulh_out), .sel(A_negative));
  // Probe on multiplier_1_out
  // Probe on multiplier_1_cout
  // Probe on mulh_out
endmodule
