// Logisim project control_logic.circ as structural Verilog: 6 circuits, main circuit control_logic
module control_logic (
  input  [31:0] inst,
  input  BrEq,
  input  BrLt,
  output PCSel,
  output RegWEn,
  output [2:0] ImmSel,
  output BrUn,
  output ASel,
  output BSel,
  output [3:0] out_10,
  output MemRW,
  output [1:0] WBSel
);

  wire and_1_out, and_2_out, B, B_PCSel, funct3_0x0, funct3_0x1, funct3_0x2, funct3_0x3, funct3_0x4,
       funct3_0x5, funct3_0x6, funct3_0x7, funct7_0x00, funct7_0x01, funct7_0x20, I, I_base, I_jalr, I_load,
       J, or_7_out, or_8_out, or_10_out, or_11_out, R, R_or_RImm, U, U_auipc, U_lui;
  wire [1:0] multiplexer_5_out, multiplexer_6_out;
  wire [2:0] multiplexer_1_out, multiplexer_2_out, multiplexer_3_out, multiplexer_4_out;

  or or_1 (R_or_RImm, R, I_base);
  opcode_decoder opcode_decoder_1 (
    .opcode(inst[6:0]), .R(R), .I_base(I_base), .I_load(I_load), .I_jalr(I_jalr), .S(MemRW), .B(B),
    .U_lui(U_lui), .U_auipc(U_auipc), .J(J));
  or or_2 (I, I_base, I_load, I_jalr);
  or or_3 (U, U_lui, U_auipc);
  funct3_decoder funct3_decoder_1 (
    .funct3(inst[14:12]), .f_0x0(funct3_0x0), .f_0x1(funct3_0x1), .f_0x2(funct3_0x2), .f_0x3(funct3_0x3),
    .f_0x4(funct3_0x4), .f_0x5(funct3_0x5), .f_0x6(funct3_0x6), .f_0x7(funct3_0x7));
  funct7_decoder funct7_decoder_1 (
    .funct7(inst[31:25]), .f_0x00(funct7_0x00), .f_0x01(funct7_0x01), .f_0x20(funct7_0x20));
  branch_for_PCSel_encoder branch_for_pcsel_encoder_1 (
    .funct3(inst[14:12]), .opcode(inst[6:0]), .BrEq(BrEq), .BrLt(BrLt), .B_for_PCSel(B_PCSel));
  Multiplexer #(.width(3), .enable("false")) multiplexer_1 (
    .in0(3'b000), .in1(3'b001), .out(multiplexer_1_out), .sel(I));
  or or_4 (RegWEn, R, I, U, J);
  Multiplexer #(.width(3), .enable("false")) multiplexer_2 (
    .in0(multiplexer_1_out), .in1(3'b010), .out(multiplexer_2_out), .sel(MemRW));
  or or_5 (ASel, B, J, U_auipc);
  or or_6 (BSel, I, MemRW, B, U, J);
  or or_7 (or_7_out, R_or_RImm, U_auipc);
  or or_8 (or_8_out, J, I_jalr);
  or or_9 (PCSel, I_jalr, B_PCSel, J);
  Multiplexer #(.width(3), .enable("false")) multiplexer_3 (
    .in0(multiplexer_2_out), .in1(3'b011), .out(multiplexer_3_out), .sel(B));
  Multiplexer #(.width(3), .enable("false")) multiplexer_4 (
    .in0(multiplexer_3_out), .in1(3'b100), .out(multiplexer_4_out), .sel(U));
  or or_10 (or_10_out, funct3_0x2, funct3_0x3);
  or or_11 (or_11_out, funct3_0x6, funct3_0x7);
  Multiplexer #(.width(2), .enable("false")) multiplexer_5 (
    .in0(2'b11), .in1(2'b00), .out(multiplexer_5_out), .sel(I_load));
  Multiplexer #(.width(2), .enable("false")) multiplexer_6 (
    .in0(multiplexer_5_out), .in1(2'b01), .out(multiplexer_6_out), .sel(or_7_out));
  // Probe on WBSel
  Multiplexer #(.width(2), .enable("false")) multiplexer_7 (
    .in0(multiplexer_6_out), .in1(2'b10), .out(WBSel), .sel(or_8_out));
  Multiplexer #(.width(3), .enable("false")) multiplexer_8 (
    .in0(multiplexer_4_out), .in1(3'b101), .out(ImmSel), .sel(J));
  and and_1 (and_1_out, R, funct7_0x00, or_10_out);
  and and_2 (and_2_out, B, or_11_out);
  ALUSel_encoder alusel_encoder_1 (.funct3(inst[14:12]), .funct7(inst[31:25]), .opcode(inst[6:0]), .ALUSel(out_10));
  or or_12 (BrUn, and_1_out, and_2_out);

  // Other names for the same wires on the sheet: ALUSel[3:0] = out_10; opcode[6:0] = inst[6:0];
  //   funct3[2:0] = inst[14:12]; funct7[6:0] = inst[31:25]; S = MemRW

  // Notes on the sheet:
  //   INPUTS to your circuit
  //   I type instruction in general
  //   U type instruction in general
  //   operation is either R type or "R-Imm" type
  //   DON'T CHANGE THE LOCATIONS OF THE INPUTS AND OUTPUTS!
  //   OUTPUT from your circuit
endmodule

module ALUSel_encoder (
  input  [2:0] funct3,
  input  [6:0] funct7,
  input  [6:0] opcode,
  output [3:0] ALUSel
);

  wire add, ADD_out, ADDI_out, and_1_out, and_2_out, and_3_out, and_4_out, and_5_out, and_6_out, and_sel,
       ANDI_out, B, divu_sel, funct3_0x0, funct3_0x1, funct3_0x2, funct3_0x3, funct3_0x4, funct3_0x5,
       funct3_0x6, funct3_0x7, funct7_0x00, funct7_0x01, funct7_0x20, I_base, I_jalr, I_load, J, LW_out, mul,
       mulh_sel, mulhu_sel, or_1_out, or_sel, ORI_out, R, remu_sel, S, sll_sel, SLLI_out, slt, sra_sel,
       SRAI_out, srl_sel, SRLI_out, sub, SW_out, U_auipc, U_lui, xor_sel, XORI_out;
  wire [3:0] multiplexer_1_out, multiplexer_2_out, multiplexer_3_out, multiplexer_4_out, multiplexer_5_out,
       multiplexer_6_out, multiplexer_7_out, multiplexer_8_out, multiplexer_9_out, multiplexer_10_out,
       multiplexer_11_out, multiplexer_12_out, multiplexer_13_out;

  opcode_decoder opcode_decoder_1 (
    .opcode(opcode), .R(R), .I_base(I_base), .I_load(I_load), .I_jalr(I_jalr), .S(S), .B(B), .U_lui(U_lui),
    .U_auipc(U_auipc), .J(J));
  funct3_decoder funct3_decoder_1 (
    .funct3(funct3), .f_0x0(funct3_0x0), .f_0x1(funct3_0x1), .f_0x2(funct3_0x2), .f_0x3(funct3_0x3),
    .f_0x4(funct3_0x4), .f_0x5(funct3_0x5), .f_0x6(funct3_0x6), .f_0x7(funct3_0x7));
  funct7_decoder funct7_decoder_1 (.funct7(funct7), .f_0x00(funct7_0x00), .f_0x01(funct7_0x01), .f_0x20(funct7_0x20));
  // Probe on ALUSel
  or or_1 (or_1_out, funct3_0x2, funct3_0x3);
  and and_1 (and_1_out, R, funct3_0x7, funct7_0x00);
  and ANDI (ANDI_out, I_base, funct3_0x7);
  and and_2 (and_2_out, R, funct3_0x6, funct7_0x00);
  and ORI (ORI_out, I_base, funct3_0x6);
  and and_3 (and_3_out, R, funct3_0x4, funct7_0x00);
  and XORI (XORI_out, I_base, funct3_0x4);
  and and_4 (and_4_out, R, funct7_0x00, funct3_0x1);
  and SLLI (SLLI_out, I_base, funct3_0x1, funct7_0x00);
  and and_5 (and_5_out, R, funct7_0x00, funct3_0x5);
  and SRLI (SRLI_out, I_base, funct3_0x5, funct7_0x00);
  and and_6 (and_6_out, R, funct7_0x20, funct3_0x5);
  and SRAI (SRAI_out, I_base, funct3_0x5, funct7_0x20);
  Multiplexer #(.width(4), .enable("false")) multiplexer_1 (
    .in0(4'b0000), .in1(4'b0000), .out(multiplexer_1_out), .sel(add));
  Multiplexer #(.width(4), .enable("false")) multiplexer_2 (
    .in0(multiplexer_1_out), .in1(4'b0001), .out(multiplexer_2_out), .sel(and_sel));
  Multiplexer #(.width(4), .enable("false")) multiplexer_3 (
    .in0(multiplexer_2_out), .in1(4'b0010), .out(multiplexer_3_out), .sel(or_sel));
  and u_ADD (ADD_out, R, funct3_0x0, funct7_0x00);
  and ADDI (ADDI_out, I_base, funct3_0x0);
  and SW (SW_out, S, funct3_0x2);
  and LW (LW_out, I_load, funct3_0x2);
  and u_MUL (mul, R, funct3_0x0, funct7_0x01);
  and u_SUB (sub, R, funct3_0x0, funct7_0x20);
  and u_SLT (slt, R, or_1_out, funct7_0x00);
  or u_AND_SEL (and_sel, and_1_out, ANDI_out);
  or u_OR_SEL (or_sel, and_2_out, ORI_out);
  or u_XOR_SEL (xor_sel, and_3_out, XORI_out);
  or u_SLL_SEL (sll_sel, and_4_out, SLLI_out);
  or u_SRL_SEL (srl_sel, and_5_out, SRLI_out);
  or u_SRA_SEL (sra_sel, and_6_out, SRAI_out);
  and DIVU (divu_sel, R, funct3_0x5, funct7_0x01);
  and REMU (remu_sel, R, funct3_0x7, funct7_0x01);
  and DIVU_2 (mulhu_sel, R, funct3_0x3, funct7_0x01);
  and REMU_2 (mulh_sel, R, funct3_0x1, funct7_0x01);
  Multiplexer #(.width(4), .enable("false")) multiplexer_4 (
    .in0(multiplexer_3_out), .in1(4'b0011), .out(multiplexer_4_out), .sel(xor_sel));
  Multiplexer #(.width(4), .enable("false")) multiplexer_5 (
    .in0(multiplexer_4_out), .in1(4'b0100), .out(multiplexer_5_out), .sel(srl_sel));
  Multiplexer #(.width(4), .enable("false")) multiplexer_6 (
    .in0(multiplexer_5_out), .in1(4'b0101), .out(multiplexer_6_out), .sel(sra_sel));
  or or_2 (add, ADD_out, ADDI_out, SW_out, LW_out);
  Multiplexer #(.width(4), .enable("false")) multiplexer_7 (
    .in0(multiplexer_6_out), .in1(4'b0110), .out(multiplexer_7_out), .sel(sll_sel));
  Multiplexer #(.width(4), .enable("false")) multiplexer_8 (
    .in0(multiplexer_7_out), .in1(4'b0111), .out(multiplexer_8_out), .sel(slt));
  Multiplexer #(.width(4), .enable("false")) multiplexer_9 (
    .in0(multiplexer_8_out), .in1(4'b1000), .out(multiplexer_9_out), .sel(divu_sel));
  Multiplexer #(.width(4), .enable("false")) multiplexer_10 (
    .in0(multiplexer_9_out), .in1(4'b1001), .out(multiplexer_10_out), .sel(remu_sel));
  Multiplexer #(.width(4), .enable("false")) multiplexer_11 (
    .in0(multiplexer_10_out), .in1(4'b1010), .out(multiplexer_11_out), .sel(mul));
  Multiplexer #(.width(4), .enable("false")) multiplexer_12 (
    .in0(multiplexer_11_out), .in1(4'b1011), .out(multiplexer_12_out), .sel(mulhu_sel));
  Multiplexer #(.width(4), .enable("false")) multiplexer_13 (
    .in0(multiplexer_12_out), .in1(4'b1100), .out(multiplexer_13_out), .sel(sub));
  Multiplexer #(.width(4), .enable("false")) multiplexer_14 (
    .in0(multiplexer_13_out), .in1(4'b1110), .out(ALUSel), .sel(mulh_sel));

  // Other names for the same wires on the sheet: result[3:0] = ALUSel
endmodule

module opcode_decoder (
  input  [6:0] opcode,
  output R,
  output I_base,
  output I_load,
  output I_jalr,
  output S,
  output B,
  output U_lui,
  output U_auipc,
  output J
);

  and and_1 (R, opcode[0], opcode[1], ~opcode[2], ~opcode[3], opcode[4], opcode[5], ~opcode[6]);  // AND_Gate
  and and_2 (I_base, opcode[0], opcode[1], ~opcode[2], ~opcode[3], opcode[4], ~opcode[5], ~opcode[6]);  // AND_Gate
  and and_3 (I_load, opcode[0], opcode[1], ~opcode[2], ~opcode[3], ~opcode[4], ~opcode[5], ~opcode[6]);  // AND_Gate
  and and_4 (I_jalr, opcode[0], opcode[1], opcode[2], ~opcode[3], ~opcode[4], opcode[5], opcode[6]);  // AND_Gate
  and and_5 (S, opcode[0], opcode[1], ~opcode[2], ~opcode[3], ~opcode[4], opcode[5], ~opcode[6]);  // AND_Gate
  and and_6 (B, opcode[0], opcode[1], ~opcode[2], ~opcode[3], ~opcode[4], opcode[5], opcode[6]);  // AND_Gate
  and and_7 (U_lui, opcode[0], opcode[1], opcode[2], ~opcode[3], opcode[4], opcode[5], ~opcode[6]);  // AND_Gate
  and and_8 (U_auipc, opcode[0], opcode[1], opcode[2], ~opcode[3], opcode[4], ~opcode[5], ~opcode[6]);  // AND_Gate
  and and_9 (J, opcode[0], opcode[1], opcode[2], opcode[3], ~opcode[4], opcode[5], opcode[6]);  // AND_Gate
endmodule

module funct3_decoder (
  input  [2:0] funct3,
  output f_0x0,
  output f_0x1,
  output f_0x2,
  output f_0x3,
  output f_0x4,
  output f_0x5,
  output f_0x6,
  output f_0x7
);

  and and_1 (f_0x0, ~funct3[0], ~funct3[1], ~funct3[2]);  // AND_Gate
  and and_2 (f_0x1, funct3[0], ~funct3[1], ~funct3[2]);  // AND_Gate
  and and_3 (f_0x2, ~funct3[0], funct3[1], ~funct3[2]);  // AND_Gate
  and and_4 (f_0x3, funct3[0], funct3[1], ~funct3[2]);  // AND_Gate
  and and_5 (f_0x4, ~funct3[0], ~funct3[1], funct3[2]);  // AND_Gate
  and and_6 (f_0x5, funct3[0], ~funct3[1], funct3[2]);  // AND_Gate
  and and_7 (f_0x6, ~funct3[0], funct3[1], funct3[2]);  // AND_Gate
  and and_8 (f_0x7, funct3[0], funct3[1], funct3[2]);
endmodule

module funct7_decoder (
  input  [6:0] funct7,
  output f_0x00,
  output f_0x01,
  output f_0x20
);

  and and_1 (f_0x00, ~funct7[0], ~funct7[1], ~funct7[2], ~funct7[3], ~funct7[4], ~funct7[5], ~funct7[6]);  // AND_Gate
  and and_2 (f_0x01, funct7[0], ~funct7[1], ~funct7[2], ~funct7[3], ~funct7[4], ~funct7[5], ~funct7[6]);  // AND_Gate
  and and_3 (f_0x20, ~funct7[0], ~funct7[1], ~funct7[2], ~funct7[3], ~funct7[4], funct7[5], ~funct7[6]);  // AND_Gate
endmodule

module branch_for_PCSel_encoder (
  input  [2:0] funct3,
  input  [6:0] opcode,
  input  BrEq,
  input  BrLt,
  output B_for_PCSel
);

  wire B, beq_out, bge_out, bgeu_out, blt_out, bltu_out, bne_out, funct3_0x0, funct3_0x1, funct3_0x2,
       funct3_0x3, funct3_0x4, funct3_0x5, funct3_0x6, funct3_0x7, I_base, I_jalr, I_load, J, R, S, U_auipc,
       U_lui;

  opcode_decoder opcode_decoder_1 (
    .opcode(opcode), .R(R), .I_base(I_base), .I_load(I_load), .I_jalr(I_jalr), .S(S), .B(B), .U_lui(U_lui),
    .U_auipc(U_auipc), .J(J));
  funct3_decoder funct3_decoder_1 (
    .funct3(funct3), .f_0x0(funct3_0x0), .f_0x1(funct3_0x1), .f_0x2(funct3_0x2), .f_0x3(funct3_0x3),
    .f_0x4(funct3_0x4), .f_0x5(funct3_0x5), .f_0x6(funct3_0x6), .f_0x7(funct3_0x7));
  and beq (beq_out, B, funct3_0x0, BrEq);
  and bne (bne_out, B, funct3_0x1, ~BrEq);  // AND_Gate
  and blt (blt_out, B, funct3_0x4, BrLt);
  and bge (bge_out, B, funct3_0x5, ~BrLt);  // AND_Gate
  and bltu (bltu_out, B, funct3_0x6, BrLt);
  and bgeu (bgeu_out, B, funct3_0x7, ~BrLt);  // AND_Gate
  or or_1 (B_for_PCSel, beq_out, bne_out, blt_out, bge_out, bltu_out, bgeu_out);
endmodule
