// Logisim project cpu.circ as structural Verilog: 1 circuit, main circuit main
module main (
  input  [31:0] INSTRUCTION,
  input  CLOCK,
  output [31:0] PROGRAM_COUNTER,
  output [31:0] ra,
  output [31:0] sp,
  output [31:0] t0,
  output [31:0] t1,
  output [31:0] t2,
  output [31:0] s0,
  output [31:0] s1,
  output [31:0] a0
);

  wire ASel, branch_comp_1_breq, branch_comp_1_brlt, BSel, control_logic_1_brun, MemRW, PCSel, RegWEn;
  wire [1:0] WBSel;
  wire [2:0] ImmSel;
  wire [3:0] control_logic_1_out_10;
  wire [31:0] A_ALU, adder_1_out, ALU_result, B_ALU, DMEM_p5, IF_ID_INSTRUCTION, imm, multiplexer_1_out,
       multiplexer_2_out, PC_IF, PC_plus_4, rs1_output, rs2_output, WB_result;

  control_logic control_logic_1 (
    .BSel(BSel), .BrUn(control_logic_1_brun), .RegWEn(RegWEn), .ImmSel(ImmSel), .ASel(ASel), .PCSel(PCSel),
    .BrLt(branch_comp_1_brlt), .BrEq(branch_comp_1_breq), .inst(IF_ID_INSTRUCTION),
    .out_10(control_logic_1_out_10), .MemRW(MemRW), .WBSel(WBSel));
  Adder #(.width(32)) adder_1 (.a(PROGRAM_COUNTER), .b(32'h4), .out(adder_1_out));  // open: cin, cout
  Multiplexer #(.width(32), .enable("false")) multiplexer_1 (
    .in0(adder_1_out), .in1(ALU_result), .out(multiplexer_1_out), .sel(PCSel));
  Register #(.width(32)) PC (.D(multiplexer_1_out), .clk(CLOCK), .Q(PROGRAM_COUNTER));  // open: en, clr
  Multiplexer #(.width(32), .enable("false")) multiplexer_2 (
    .in0(INSTRUCTION), .in1(32'h13), .out(multiplexer_2_out), .sel(PCSel));
  Register #(.width(32)) u_PC_IF (.D(PROGRAM_COUNTER), .clk(CLOCK), .Q(PC_IF));  // open: en, clr
  imm_gen imm_gen_1 (.ImmSel(ImmSel), .inst(IF_ID_INSTRUCTION), .imm(imm));
  // Probe on imm
  // Probe on IF_ID_INSTRUCTION
  // Probe on RegWEn
  Register #(.width(32)) u_IF_ID_INSTRUCTION (
    .D(multiplexer_2_out), .clk(CLOCK), .Q(IF_ID_INSTRUCTION));  // open: en, clr
  // Probe on ImmSel
  // Probe on rs1_output
  regfile_main RegFile (
    .rs2(IF_ID_INSTRUCTION[24:20]), .rd(IF_ID_INSTRUCTION[11:7]), .Read_Data_1(rs1_output),
    .Read_Data_2(rs2_output), .ra(ra), .sp(sp), .t0(t0), .t1(t1), .t2(t2), .s0(s0), .s1(s1), .a0(a0),
    .rs1(IF_ID_INSTRUCTION[19:15]), .Write_Data(WB_result), .RegWEn(RegWEn), .clk(CLOCK));
  // Probe on rs2_output
  branch_comp branch_comp_1 (
    .BrEq(branch_comp_1_breq), .BrLt(branch_comp_1_brlt), .BrUn(control_logic_1_brun));  // open: rs1, rs2
  // Probe on ASel
  Multiplexer #(.width(32), .enable("false")) multiplexer_3 (.in0(rs1_output), .in1(PC_IF), .out(A_ALU), .sel(ASel));
  Multiplexer #(.width(32), .enable("false")) multiplexer_4 (.in0(rs2_output), .in1(imm), .out(B_ALU), .sel(BSel));
  // Probe on A_ALU
  // Probe on B_ALU
  alu Arithmetic_Logic_Unit (.ALUSel(control_logic_1_out_10), .Result(ALU_result), .A(A_ALU), .B(B_ALU));
  // Probe on BSel
  // Probe on ALU_result
  // Probe on control_logic_1_out_10
  // Probe on MemRW
  // mem_main DMEM: pin names not known; wires that end beside it: ALU_result, rs2_output, CLOCK, MemRW, DMEM_p5
  Adder #(.width(32)) adder_2 (.a(PC_IF), .b(32'h4), .out(PC_plus_4));  // open: cin, cout
  // Probe on DMEM_p5
  // Probe on WB_result
  Multiplexer #(.select(2), .width(32), .enable("false")) multiplexer_5 (
    .in0(DMEM_p5), .in1(ALU_result), .in2(PC_plus_4), .in3(imm), .out(WB_result), .sel(WBSel));
  // Probe on WBSel

  // Other names for the same wires on the sheet: clk = CLOCK; rd_5[4:0] = IF_ID_INSTRUCTION[11:7];
  //   rs1_5[4:0] = IF_ID_INSTRUCTION[19:15]; rs2_5[4:0] = IF_ID_INSTRUCTION[24:20]

  // Notes on the sheet:
  //   Control Hazard: instruction killer
  //   Output
  //   IMEM (do **NOT** move this)
  //   Inputs
  //   Pipeline IF/ID
  //   It is OK to move the PC, RegFile, ALU, MEM, Branch Comp, Imm Gen, and Control Logic to wherever is most convenient for you when constructing your CPU, and to delete this text
  //   Inputs/Outputs for testing. Do **NOT** move these.
  //   Write back the imm when WBSel = 3 (lui rd, offset)
endmodule
