// Logisim project imm_gen.circ as structural Verilog: 3 circuits, main circuit imm_gen
module imm_gen (
  input  [31:0] inst,
  input  [2:0] ImmSel,
  output [31:0] imm
);

  wire [31:0] B_imm, I_imm, S_imm;

  // Probe on imm
  Multiplexer #(.select(3), .width(32), .enable("false")) multiplexer_1 (
    .in0({32{1'b0}}), .in1(I_imm), .in2(S_imm), .in3(B_imm), .in4({{12{1'b0}}, inst[31:12]}),
    .in5({{12{1'b0}}, inst[31], inst[19:12], inst[20], inst[30:21]}), .out(imm), .sel(ImmSel));  // open: in6, in7
  Imm_12_32_extensor imm_12_32_extensor_1 (.bits_imm_12(inst[31:20]), .imm_32_bits(I_imm));
  Imm_12_32_extensor imm_12_32_extensor_2 (.bits_imm_12({inst[31:25], inst[11:7]}), .imm_32_bits(S_imm));
  Imm_12_32_extensor imm_12_32_extensor_3 (
    .bits_imm_12({inst[31], inst[7], inst[30:25], inst[11:8]}), .imm_32_bits(B_imm));
  // Probe on I_imm
  // Probe on S_imm
  // Probe on B_imm
  // Probe on {{12{1'b0}}, inst[31:12]}
  // Probe on {{12{1'b0}}, inst[31], inst[19:12], inst[20], inst[30:21]}

  // Other names for the same wires on the sheet: opcode[6:0] = inst[6:0];
  //   J_imm[19:0] = {inst[31], inst[19:12], inst[20], inst[30:21]}; U_imm[19:0] = inst[31:12];
  //   funct3[2:0] = inst[14:12]

  // Notes on the sheet:
  //   INPUTS to your circuit
  //   DON'T CHANGE THE LOCATIONS OF THE INPUTS AND OUTPUTS!
  //   OUTPUT from your circuit
endmodule

module Imm_12_32_extensor (
  input  [11:0] bits_imm_12,
  output [31:0] imm_32_bits
);

  // Probe on {{21{bits_imm_12[11]}}, bits_imm_12[10:0]}

  assign imm_32_bits = {{21{bits_imm_12[11]}}, bits_imm_12[10:0]};
endmodule

module imm_12_bits (
  input  [31:0] instruction,
  output [4:0] bits_0_4,
  output [6:0] bits_5_11,
  output [11:0] bits_0_11,
  output bit_11
);


  assign bit_11 = instruction[31];
  assign bits_0_4 = instruction[24:20];
  assign bits_0_11 = instruction[31:20];
  assign bits_5_11 = instruction[31:25];
endmodule
